# Fritzing sketch neopixelArduino (saved by Fritzing 0.9.3b)

parts:
  Componente1 = Arduino Uno (Rev3)
  U1 = WS2812 RGB LED strip

nets:
  N1: Componente1.D2, U1.DIN
  5V: Componente1.5V, U1.VCC
  GND: Componente1.GND, U1.GND

custom parts:
  WS2812 RGB LED strip: WS2812 strip
